# Fritzing sketch Comunicacion_arduino_java (saved by Fritzing 0.9.3b)
breadboards: 1

parts:
  Componente1 = Arduino Uno (Rev3)
  LCD1 = LCD screen
  RHT1 = Humidity and Temperature Sensor RHT03
  R1 = Rotary Potentiometer (Small) [maximum_resistance=100kΩ package=THT]
  R2 = Resistor [tolerance=±5% resistance=220 package=THT]
  R3 = Resistor [tolerance=±5% resistance=220 package=THT]

nets:
  N1: Componente1.D11_PWM/MOSI, LCD1.E
  N2: Componente1.D12/MISO, LCD1.RS
  N3: Componente1.D2, LCD1.DB7
  N4: Componente1.D3_PWM, LCD1.DB6
  N5: Componente1.D4, LCD1.DB5
  N6: Componente1.D5_PWM, LCD1.DB4
  N7: Componente1.D7, R2.Pin_0
  5V: Componente1.5V, LCD1.VDD, RHT1.Vcc, R1.leg2
  GND: Componente1.GND, LCD1.VSS, LCD1.R/W, LCD1.LED-, RHT1.GND_2
  N8: LCD1.V0, R1.wiper
  N9: LCD1.LED+, R3.Pin_0
  N10: RHT1.GND_1, R2.Pin_1

notes:
  Comunicación Arduino y Java por puerto Serial.

// code stored in the sketch: Comunicacion_arduino_java.ino
//Llamamos a la libreria de los sensores DHT instalada previamente
#include <dht.h>

//Llamamos a la libreria para controlar el LCD incluida en el IDE de Arduino
#include <LiquidCrystal.h>

//Definimos los pines asignados al LCD según el esquema de conexión
LiquidCrystal lcd(12, 11, 5, 4, 3, 2);

//definimos el objeto para poder traer el dato del sensor DHT11
dht DHT;

//Definimos el pin de Arduino al que conectamos el pin de datos del sensor e indicamos el tipo de sensor (DHT11)
#define DHT11_PIN 7

//iniciamos la variable que leara el dato de la comunicacion
String entrada;

//Definimos las variables del reloj
int mit = 45, seg=1, hor=9;

//Definimos la variable del contador
int cont=1;

//Definimos las variables de la fecha
int dia=18,mes=4,ano=2018;

void setup(){    
  //Iniciamos la comunicacion del serial
  Serial.begin(9600);

  //Indicamos el LCD que usamos: 16 caracteres y 2 lineas
  lcd.begin(16, 2);
}

void loop(){
  //Aqui se despliega la temperatura y humedad en el display
  if(cont == 1){
    //limpiar el display
    lcd.clear();
    //Mostramos la información obtenida (temperatura y humedad) en el Monitor Serial
    int chk = DHT.read11(DHT11_PIN);
    //Situamos el cursor en la posicion 0 de la primera linea
    lcd.setCursor(0,0); 
    lcd.print("Temp:");
    lcd.print(DHT.temperature);    
    //Editamos el simbolo de los grados º
    lcd.print((char)223);
    lcd.print("C");
    lcd.setCursor(0,1);
    lcd.print("Hum:");
    lcd.print(DHT.humidity);
    lcd.print("%");  
  }
  //Aqui se despliega la hora y fecha en el display
  if(cont == 2){    
    //Iniciamos el contador del segundos para que empiece a contar los segundos y inicie tambien el reloj  
    seg++;    
    if(seg > 59){
      mit++;
      seg=0;  
    }
    if(mit > 59){
      hor++;
      mit=0;  
    }
    if(hor == 23 && mit == 59 && seg == 59){
      dia++;
    }
    if(dia == 31 || mes == 1 || mes == 3 || mes == 5 || mes == 7 || mes == 8 || mes == 10 && hor == 23 && mit == 59 && seg == 59){
      mes++;
      dia=1;  
    }else if(dia == 30 || mes == 4 || mes == 6 || mes == 9 && hor == 23 && mit == 59 && seg == 59){
      mes++;
      dia=1;
    }else if(dia == 28 && mes == 2 && hor == 23 && mit == 59 && seg == 59){
      mes++;
      dia=1;
    }
    if(dia == 31 && mes == 12 && hor == 23 && mit == 59 && seg == 59){
      ano++;
      mes=1;
    }
    //Limpiar el display
    lcd.clear();
    //Mostramos la información obtenida (temperatura y humedad) en el Monitor Serial
    int chk = DHT.read11(DHT11_PIN);
    //Situamos el cursor en la posicion 0 de la primera linea
    lcd.setCursor(0,0); 
    lcd.print("HORA: ");
    if(hor < 10){        
      lcd.print("0");      
    }
    lcd.print(hor);
    lcd.print(":");
    if(mit < 10){
      lcd.print("0");
    }    
    lcd.print(mit);
    if(hor<12){
      lcd.print(" AM");
    }else{
      lcd.print(" PM"); 
    }

    lcd.setCursor(0,1);
    lcd.print("Fecha:");
    lcd.print(dia);
    lcd.print("/");
    lcd.print(mes);
    lcd.print("/");
    lcd.print(ano);    
  }
  //Aqui se despliega el mensaje en el display
  if(cont == 3){
    //Se manda al metodo Decimal_to_ASCII el dato que recibe por el serial
    while(Serial.available()>0){
      entrada = entrada+Decimal_to_ASCII(Serial.read());  
    }
    //Limpiar el display
    lcd.clear();
    lcd.setCursor(0,0);
    lcd.print("Bienvenido"); 

    //Se guarda el tamaño de la vaiable
    int contador = entrada.length();
    for(int i = contador;i>0;i--){
      //extraemos los caracteres
      String texto = entrada.substring(i-1);  

      //Situamos el cursor
      lcd.setCursor(0,1); 
      //Escribimos el texto   
      lcd.print(texto);           
      //Esperamos
      delay(350);
    }  
    //Limpia la Variable de entrada
      entrada=" ";
        
  }
  if(cont == 4){
    cont = 0;
  }  
  
  //lee la temperatura desde el sensor
  float t = DHT.temperature;
  float h = DHT.humidity;
      
  //float f = ((9/5) * t)+32;
  //Serial.println(f);      
  //Serial.println(h);
  
  //Se manda el valor por el Serial
  Serial.println(t);   

  cont++;
  delay(1500);
   

}

/*Creamos este metodo para poder trasnformar la entrada que recibe en codigo ASCII
Ponerlo el caracter que tiene en el lenguaje ASCII*/
char Decimal_to_ASCII(int entrada){
  char salida=' ';
  switch(entrada){
    case 32: 
      salida=' '; 
    break; 
    case 33: 
      salida='!'; 
    break; 
    case 34: 
      salida='"'; 
    break; 
    case 35: 
      salida='#'; 
    break; 
    case 36: 
      salida='$'; 
    break; 
    case 37: 
      salida='%'; 
    break; 
    case 38: 
      salida='&'; 
    break; 
    case 39: 
      salida=' '; 
    break; 
    case 40: 
      salida='('; 
    break; 
    case 41: 
      salida=')'; 
    break; 
    case 42: 
      salida='*'; 
    break; 
    case 43: 
      salida='+'; 
    break; 
    case 44: 
      salida=','; 
    break; 
    case 45: 
      salida='-'; 
    break; 
    case 46: 
      salida='.'; 
    break; 
    case 47: 
      salida='/'; 
    break; 
    case 48: 
      salida='0'; 
    break; 
    case 49: 
      salida='1'; 
    break; 
    case 50: 
      salida='2'; 
    break; 
    case 51: 
      salida='3'; 
    break; 
    case 52: 
      salida='4'; 
    break; 
    case 53: 
      salida='5'; 
    break; 
    case 54: 
      salida='6'; 
    break; 
    case 55: 
      salida='7'; 
    break; 
    case 56: 
      salida='8'; 
    break; 
    case 57: 
      salida='9'; 
    break; 
    case 58: 
      salida=':'; 
    break; 
    case 59: 
      salida=';'; 
    break; 
    case 60: 
      salida='<'; 
    break; 
    case 61: 
      salida='='; 
    break; 
    case 62: 
      salida='>'; 
    break; 
    case 63: 
      salida='?'; 
    break; 
    case 64: 
      salida='@'; 
    break; 
    case 65: 
      salida='A'; 
    break; 
    case 66: 
      salida='B'; 
    break; 
    case 67: 
      salida='C'; 
    break; 
    case 68: 
      salida='D'; 
    break; 
    case 69: 
      salida='E'; 
    break; 
    case 70: 
      salida='F'; 
    break; 
    case 71: 
      salida='G'; 
    break; 
    case 72: 
      salida='H'; 
    break; 
    case 73: 
      salida='I'; 
    break; 
    case 74: 
      salida='J'; 
    break; 
    case 75: 
      salida='K'; 
    break; 
    case 76: 
      salida='L'; 
    break; 
    case 77: 
      salida='M'; 
    break; 
    case 78: 
      salida='N'; 
    break; 
    case 79: 
      salida='O'; 
    break; 
    case 80: 
      salida='P'; 
    break; 
    case 81: 
      salida='Q'; 
    break; 
    case 82: 
      salida='R'; 
    break; 
    case 83: 
      salida='S'; 
    break; 
    case 84: 
      salida='T'; 
    break; 
    case 85: 
      salida='U'; 
    break; 
    case 86: 
      salida='V'; 
    break; 
    case 87: 
      salida='W'; 
    break; 
    case 88: 
      salida='X'; 
    break; 
    case 89: 
      salida='Y'; 
    break; 
    case 90: 
      salida='Z'; 
    break; 
    case 91: 
      salida='['; 
    break; 
    case 92: 
      salida=' '; 
    break; 
    case 93: 
      salida=']'; 
    break; 
    case 94: 
      salida='^'; 
    break; 
    case 95: 
      salida='_'; 
    break; 
    case 96: 
      salida='`'; 
    break; 
    case 97: 
      salida='a'; 
    break; 
    case 98: 
      salida='b'; 
    break; 
    case 99: 
      salida='c'; 
    break; 
    case 100: 
      salida='d'; 
    break; 
    case 101: 
      salida='e'; 
    break; 
    case 102: 
      salida='f'; 
    break; 
    case 103: 
      salida='g'; 
    break; 
    case 104: 
      salida='h'; 
    break; 
    case 105: 
      salida='i'; 
    break; 
    case 106: 
      salida='j'; 
    break; 
    case 107: 
      salida='k'; 
    break; 
      case 108: 
    salida='l'; 
    break; 
    case 109: 
      salida='m'; 
    break; 
    case 110: 
      salida='n'; 
    break; 
    case 111: 
      salida='o'; 
    break; 
    case 112: 
      salida='p'; 
    break; 
    case 113: 
      salida='q'; 
    break; 
    case 114: 
      salida='r'; 
    break; 
    case 115: 
      salida='s'; 
    break; 
    case 116: 
      salida='t'; 
    break; 
    case 117: 
      salida='u'; 
    break; 
    case 118: 
      salida='v'; 
    break; 
    case 119: 
      salida='w'; 
    break; 
    case 120: 
      salida='x'; 
    break; 
    case 121: 
      salida='y'; 
    break; 
    case 122: 
      salida='z'; 
    break; 
    case 123: 
      salida='{'; 
    break; 
    case 124: 
      salida='|'; 
    break; 
    case 125: 
      salida='}'; 
    break; 
    case 126: 
      salida='~'; 
    break; 
  }
return salida;
}
